# Fritzing sketch alim (saved by Fritzing 0.9.0b)
circuit board: 2.8cm x 2.8cm
perfboards: 1

parts:
  R200 = Resistor [tolerance=±5% resistance=220 package=THT]
  C470uF = Electrolytic Capacitor [capacitance=1µF package="100 mil [THT, electrolytic]"]
  C470uF_2 = Electrolytic Capacitor [capacitance=1µF package="100 mil [THT, electrolytic]"]
  J2 = female pin header, 2 pins [form="♀ (female)"]
  J3 = female pin header, 2 pins [form="♀ (female)"]
  L7805 = Voltage Regulator [package=to220-adj]
  LED = LED - 3mm [color="Red (633nm)" package="3 mm [THT]"]
  J4 = male pin header, 1 pin [form="♂ (male)"]
  J5 = screw terminal, 2 pins
  AMS117 = Voltage Regulator [package=to220-adj]
  C47uF = Electrolytic Capacitor [capacitance=1µF package="100 mil [THT, electrolytic]"]

nets:
  N1: R200.Pin_0, J2.pin2, AMS117.OUT, C47uF.+
  N2: R200.Pin_1, LED.cathode
  N3: C470uF.-, C470uF_2.-, J2.pin1, J3.pin2, L7805.OUT, LED.anode, J4.pin1, J5.pin1, AMS117.ADJ, C47uF.-
  N4: C470uF.+, L7805.IN, J5.pin2
  N5: C470uF_2.+, J3.pin1, L7805.ADJ, AMS117.IN
