# Fritzing sketch atmega_bb (saved by Fritzing 0.9.0b)
breadboards: 1

parts:
  Y1 = CRYSTAL [package=crystal-smd-10.5x4.8-2pin]
  IC1 = MICROCONTROLLER [package=dil28-3]
  C2 = Capacitor [package=cap-pth-small2]
  R1 = Resistor [tolerance=±5% resistance=10k package=THT]
  R2 = Resistor [tolerance=±5% resistance=330 package=THT]
  LED1 = LED - 3mm [color="Red (633nm)" package="3 mm [THT]"]
  C1 = Capacitor [package=cap-pth-small2]

nets:
  N1: Y1.1, IC1.PB7(XTAL2_TOSC2), C2.2
  N2: Y1.2, IC1.PB6(XTAL1_TOSC1), C1.1
  N3: IC1.PC6(_RESET), R1.Pin_0
  N4: IC1.VCC, IC1.AVCC, R1.Pin_1
  N5: IC1.GND, IC1.AGND, C2.1, R2.Pin_0, C1.2
  N6: IC1.PB5(SCK), LED1.anode
  N7: R2.Pin_1, LED1.cathode
