# Fritzing sketch temp (saved by Fritzing 0.9.0b)
circuit board: 10.8325cm x 4.10326cm
circuit board: 2.54cm x 2.54cm
circuit board: 2.54cm x 2.54cm
breadboards: 1

parts:
  IC1 = MICROCONTROLLER [package=dil28-3]
  LED1 = LED - 3mm [color="Red (633nm)" package="3 mm [THT]"]
  J2 = female pin header, 2 pins [form="♀ (female)"]
  J1 = female pin header, 2 pins [form="♀ (female)"]
  R1 = Resistor [tolerance=±5% resistance=10k package=THT]
  R2 = Resistor [tolerance=±5% resistance=330 package=THT]
  XTAL1 = Crystal [frequency="16 Mhz" package=THT]
  T1 = LM35 Temperature Sensor [package="TO92 [THT]"]
  R3 = Resistor [tolerance=±5% resistance=4.7k package=THT]
  C1 = Capacitor [package=cap-pth-small2]
  C2 = Capacitor [package=cap-pth-small2]
  J4 = female pin header, 1 pin [form="♀ (female)"]
  J6 = female pin header, 1 pin [form="♀ (female)"]
  J7 = female pin header, 1 pin [form="♀ (female)"]  # not connected
  J8 = female pin header, 1 pin [form="♀ (female)"]  # not connected
  J3 = female pin header, 2 pins [form="♀ (female)"]
  J5 = female pin header, 1 pin [form="♀ (female)"]  # not connected

nets:
  N1: IC1.VCC, J2.pin2, R2.Pin_0, C1.2, C2.2
  N2: IC1.PB6(XTAL1_TOSC1), R1.Pin_1, T1.GND, R3.Pin_1
  N3: IC1.PB7(XTAL2_TOSC2), LED1.cathode
  N4: IC1.PB5(SCK), XTAL1.pin_0, C1.1
  N5: IC1.AVCC, XTAL1.pin_1, C2.1
  N6: IC1.AREF, J1.pin1, J4.pin1
  N7: IC1.AGND, J1.pin2
  N8: IC1.PC2(ADC2), T1.Vout, R3.Pin_0
  N9: IC1.PC3(ADC3), J3.pin1
  N10: IC1.PC4(ADC4_SDA), J3.pin2
  N11: IC1.PC5(ADC5_SCL), R1.Pin_0
  N12: LED1.anode, R2.Pin_1
  N13: J2.pin1, J6.pin1
