# Fritzing sketch isp (saved by Fritzing 0.9.0b)
circuit board: 3.3cm x 5.58cm
perfboards: 1

parts:
  Socket28pin = MICROCONTROLLER [package=dil28-3-simon]
  J1 = male pin header, 8 pins [form="♂ (male)"]
  R10K = Resistor [tolerance=±5% resistance=10k package=THT]
  16Mhz = Crystal [frequency="16 Mhz" package=THT]
  J2 = male pin header, 6 pins [form="♂ (male)"]
  C22pf = Capacitor [package=cap-pth-small2]
  C22pf_2 = Capacitor [package=cap-pth-small2]

nets:
  N1: Socket28pin.VCC, Socket28pin.AREF, J2.pin3, C22pf.1, C22pf_2.1
  N2: Socket28pin.PB6(XTAL1_TOSC1), Socket28pin.AGND, R10K.Pin_1, J2.pin4
  N3: Socket28pin.PB7(XTAL2_TOSC2), J1.pin6
  N4: Socket28pin.PD5(T1), J1.pin5
  N5: Socket28pin.PD6(AIN0), J1.pin4
  N6: Socket28pin.PB5(SCK), 16Mhz.pin_1, C22pf_2.2
  N7: Socket28pin.AVCC, 16Mhz.pin_0, C22pf.2
  N8: Socket28pin.PC5(ADC5_SCL), J1.pin3, R10K.Pin_0
